// Logisim project ALU.circ as structural Verilog: 1 circuit, main circuit ALU
module ALU (
  input  [31:0] A,
  input  [31:0] B,
  input  [4:0] Shift,
  input  [3:0] Codop,
  input  CarryIn,
  output [31:0] S,
  output [3:0] Flags
);

  wire C_ADC, C_CMN, C_CMP, C_RSB, C_SBC, undriven, undriven_2, undriven_3, undriven_4, undriven_5,
       undriven_6, undriven_7, undriven_8, undriven_9, V;
  wire [31:0] ADC, ASR, BIC, bit_extender_1_out, CMN, CMP, EOR, ET, LSL, LSR, MUL, MVN, not_1_out, ORR, R,
       RSB, SBC, subtractor_1_out, subtractor_2_out, TST;

  assign bit_extender_1_out = {{31{CarryIn}}, CarryIn};  // Bit_Extender bit_extender_1
  assign not_1_out = ~A;  // NOT_Gate not_1, 32 bits wide
  assign ET = A & B;  // AND_Gate and_1, 32 bits wide
  assign EOR = A ^ B;  // XOR_Gate xor_1, 32 bits wide
  Shifter #(.width(32)) shifter_1 (.in(B), .\dist (Shift), .out(LSL));
  Shifter #(.shift("lr"), .width(32)) shifter_2 (.in(B), .\dist (Shift), .out(LSR));
  Shifter #(.shift("ar"), .width(32)) shifter_3 (.in(B), .\dist (Shift), .out(ASR));
  Adder #(.width(32)) adder_1 (.a(A), .b(B), .out(ADC), .cin(CarryIn), .cout(C_ADC));
  Subtractor #(.width(32)) subtractor_1 (.a(B), .b(A), .out(subtractor_1_out));  // open: bin, bout
  Subtractor #(.width(32)) subtractor_2 (.a(bit_extender_1_out), .b(32'h1), .out(subtractor_2_out));  // open: bin, bout
  Shifter #(.shift("rr"), .width(32)) shifter_4 (.in(B), .\dist (Shift), .out(R));
  assign TST = A & B;  // AND_Gate and_2, 32 bits wide
  Subtractor #(.width(32)) subtractor_3 (.a({32{1'b0}}), .b(A), .out(RSB), .bout(C_RSB));  // open: bin
  Subtractor #(.width(32)) subtractor_4 (.a(B), .b(A), .out(CMP), .bout(C_CMP));  // open: bin
  Adder #(.width(32)) adder_2 (.a(A), .b(B), .out(CMN), .cout(C_CMN));  // open: cin
  assign ORR = A | B;  // OR_Gate or_1, 32 bits wide
  Multiplier #(.width(32)) multiplier_1 (.a(A), .b(B), .out(MUL));  // open: cin, cout
  assign BIC = B & not_1_out;  // AND_Gate and_3, 32 bits wide
  assign MVN = ~A;  // NOT_Gate not_2, 32 bits wide
  Adder #(.width(32)) adder_3 (.a(subtractor_1_out), .b(subtractor_2_out), .out(SBC), .cout(C_SBC));  // open: cin
  Multiplexer #(.enable("true"), .select(4), .width(32)) multiplexer_1 (
    .in0(ET), .in1(EOR), .in2(LSL), .in3(LSR), .in4(ASR), .in5(ADC), .in6(SBC), .in7(R), .in9(RSB),
    .in12(ORR), .in13(MUL), .in14(BIC), .in15(MVN), .out(S), .sel(Codop));  // open: in8, in10, in11, en
  Multiplexer #(.enable("true"), .select(4)) multiplexer_2 (
    .in0(1'b0), .in1(1'b0), .in2(undriven_8), .in3(undriven_6), .in4(undriven_9), .in5(C_ADC), .in6(C_SBC),
    .in7(undriven_7), .in8(1'b0), .in9(C_RSB), .in10(C_CMP), .in11(C_CMN), .in12(1'b0), .in13(1'b0),
    .in14(1'b0), .in15(1'b0), .out(Flags[2]), .sel(Codop));  // open: en
  Multiplexer #(.enable("true"), .select(4)) multiplexer_3 (
    .in0(1'b0), .in1(1'b0), .in2(1'b0), .in3(1'b0), .in4(1'b0), .in5(undriven_3), .in6(undriven), .in7(1'b0),
    .in8(1'b0), .in9(undriven_4), .in10(undriven_2), .in11(undriven_5), .in12(1'b0), .in13(1'b0),
    .in14(1'b0), .in15(1'b0), .out(V), .sel(Codop));  // open: en
  Comparator #(.width(32)) comparator_1 (.b({32{1'b1}}));  // open: a, gt, eq, lt
  Comparator #(.width(32)) comparator_2 (.a(S), .b({32{1'b0}}), .eq(Flags[1]), .lt(Flags[0]));  // open: gt

  // Other names for the same wires on the sheet: CIn = CarryIn; Co[3:0] = Codop; N = Flags[0]; Z = Flags[1];
  //   C = Flags[2]; S_t[4:0] = Shift

  // Notes on the sheet:
  //   Note: for ROR, C = N
  //   Note 2: assume that shift > 0 for LSL and LSR
endmodule
