// Logisim project Ctl_Opcode_Decoder.circ as structural Verilog: 1 circuit, main circuit Opcode_Decoder
module Opcode_Decoder (
  input  [5:0] Opcode,
  output Shift,
  output Data_Processing,
  output Load_Store,
  output SP_Address,
  output Conditional
);

  SR_OCDECODE sr_ocdecode_1 (
    .Opcode(Opcode), .Shift(Shift), .Data_Processing(Data_Processing), .Load_Store(Load_Store),
    .SP_Address(SP_Address), .Conditional(Conditional));

  // Notes on the sheet:
  //   Shift, add, sub, mov
  //   Load/Store
  //   SP Address
  //   Data Processing
  //   Conditional branch
endmodule
